// Digital circuit multiplier.dig as structural Verilog
module multiplier (
  input  A0,
  input  A1,
  input  A2,
  input  A3,
  input  B0,
  input  B2,
  input  B3,
  input  B1,
  output Z0,
  output Z1,
  output Z2,
  output Z3,
  output Z4,
  output Z5,
  output Z6,
  output Z7
);

  wire add_1_c_o, add_1_s, add_2_c_o, add_2_s, add_3_c_o, add_3_s, add_4_c_o, add_4_s, add_5_c_o, add_5_s,
       add_6_c_o, add_7_c_o, and_2_out, and_3_out, and_4_out, and_5_out, and_6_out, and_7_out, and_8_out,
       and_9_out, and_10_out, and_11_out, and_12_out, and_13_out, and_14_out, and_15_out, and_16_out,
       half_adder_1_p4, half_adder_2_p3, half_adder_2_p4, half_adder_3_p4, half_adder_4_p4;

  and and_1 (Z0, A0, B0);
  and and_2 (and_2_out, A1, B0);
  and and_3 (and_3_out, A2, B0);
  and and_4 (and_4_out, A3, B0);
  and and_5 (and_5_out, A0, B1);
  and and_6 (and_6_out, A1, B1);
  and and_7 (and_7_out, A2, B1);
  and and_8 (and_8_out, A3, B1);
  and and_9 (and_9_out, A0, B2);
  and and_10 (and_10_out, A1, B2);
  and and_11 (and_11_out, A2, B2);
  and and_12 (and_12_out, A3, B2);
  and and_13 (and_13_out, A0, B3);
  and and_14 (and_14_out, A1, B3);
  and and_15 (and_15_out, A2, B3);
  and and_16 (and_16_out, A3, B3);
  // Half_Adder half_adder_1: pin names not known; wires that end beside it: and_2_out, and_5_out, Z1, half_adder_1_p4
  Add add_1 (.a(and_3_out), .b(and_6_out), .c_i(half_adder_1_p4), .s(add_1_s), .c_o(add_1_c_o));
  Add add_2 (.a(and_4_out), .b(and_7_out), .c_i(add_1_c_o), .s(add_2_s), .c_o(add_2_c_o));
  // Half_Adder half_adder_2: pin names not known; wires that end beside it: add_2_c_o, and_8_out, half_adder_2_p3, half_adder_2_p4
  // Half_Adder half_adder_3: pin names not known; wires that end beside it: add_1_s, and_9_out, Z2, half_adder_3_p4
  Add add_3 (.a(add_2_s), .b(and_10_out), .c_i(half_adder_3_p4), .s(add_3_s), .c_o(add_3_c_o));
  Add add_4 (.a(half_adder_2_p3), .b(and_11_out), .c_i(add_3_c_o), .s(add_4_s), .c_o(add_4_c_o));
  Add add_5 (.a(half_adder_2_p4), .b(and_12_out), .c_i(add_4_c_o), .s(add_5_s), .c_o(add_5_c_o));
  // Half_Adder half_adder_4: pin names not known; wires that end beside it: add_3_s, and_13_out, Z3, half_adder_4_p4
  Add add_6 (.a(add_4_s), .b(and_14_out), .c_i(half_adder_4_p4), .s(Z4), .c_o(add_6_c_o));
  Add add_7 (.a(add_5_s), .b(and_15_out), .c_i(add_6_c_o), .s(Z5), .c_o(add_7_c_o));
  Add add_8 (.a(add_5_c_o), .b(and_16_out), .c_i(add_7_c_o), .s(Z6), .c_o(Z7));
endmodule
